# Fritzing sketch Herba-Automata (saved by Fritzing 0.9.3b)
breadboards: 1

parts:
  Part1 = Arduino Nano (Rev3.0)
  DHT1 = DHT11 Humitidy and Temperature Sensor
  Part2 = Soil Moisture Sensor
  U1 = 4-Channel 5v Relay Shield [package=relay-4ch5v10a]

nets (from the schematic view):
  GND: Part1.GND, DHT1.GND, Part2.GND, U1.GND
  N1: Part1.D2, DHT1.DATA
  N2: Part1.D3, Part2.SIG
  N3: Part1.D4, U1.K1-On, U1.K3-On
  5V: Part1.VIN, DHT1.VDD, Part2.VCC

custom parts:
  DHT11 Humitidy and Temperature Sensor: DHT11 Humidity and Temperature Sensor
  4-Channel 5v Relay Shield: 4 Channel 5v Relay Shield w. 2x SPD-06VDC-SD-C

// code stored in the sketch: Herba-Automata.ino
void setup() {
  // put your setup code here, to run once:

}

void loop() {
  // put your main code here, to run repeatedly:

}
